// Logisim project ALU_cricuits.circ as structural Verilog: 1 circuit, main circuit main
module main (
  input  [15:0] in_1,
  input  zx,
  input  nx,
  input  zy,
  input  ny,
  input  f,
  input  no,
  input  [15:0] x_i,
  input  [15:0] y_i,
  output zr,
  output [15:0] out_11,
  output [15:0] \output ,
  output [15:0] out_13,
  output ng
);

  wire adder_1_cout, or_6_out;
  wire [15:0] adder_1_out, and_1_out, and_2_out, and_3_out, multiplexer_1_out, multiplexer_2_out,
       multiplexer_5_out, not_1_out, not_2_out, not_3_out, or_1_out, or_2_out, or_3_out, or_4_out, or_5_out;

  assign or_1_out = x_i | in_1;  // OR_Gate or_1, 16 bits wide
  Multiplexer #(.width(16), .enable("false")) multiplexer_1 (
    .in0(or_1_out), .in1(and_1_out), .out(multiplexer_1_out), .sel(zx));
  assign and_1_out = x_i & in_1;  // AND_Gate and_1, 16 bits wide
  assign or_2_out = y_i | in_1;  // OR_Gate or_2, 16 bits wide
  assign and_2_out = y_i & in_1;  // AND_Gate and_2, 16 bits wide
  assign or_3_out = multiplexer_1_out | in_1;  // OR_Gate or_3, 16 bits wide
  assign not_1_out = ~multiplexer_1_out;  // NOT_Gate not_1, 16 bits wide
  Multiplexer #(.width(16), .enable("false")) multiplexer_2 (
    .in0(or_2_out), .in1(and_2_out), .out(multiplexer_2_out), .sel(zy));
  assign not_2_out = ~multiplexer_2_out;  // NOT_Gate not_2, 16 bits wide
  Multiplexer #(.width(16), .enable("false")) multiplexer_3 (.in0(or_3_out), .in1(not_1_out), .out(out_11), .sel(nx));
  assign or_4_out = multiplexer_2_out | in_1;  // OR_Gate or_4, 16 bits wide
  Multiplexer #(.width(16), .enable("false")) multiplexer_4 (.in0(or_4_out), .in1(not_2_out), .out(out_13), .sel(ny));
  assign and_3_out = out_11 & out_13;  // AND_Gate and_3, 16 bits wide
  Adder #(.width(16)) adder_1 (.a(out_11), .b(out_13), .out(adder_1_out), .cout(adder_1_cout));  // open: cin
  Multiplexer #(.width(16), .enable("false")) multiplexer_5 (
    .in0(and_3_out), .in1(adder_1_out), .out(multiplexer_5_out), .sel(f));
  assign not_3_out = ~multiplexer_5_out;  // NOT_Gate not_3, 16 bits wide
  assign or_5_out = multiplexer_5_out | in_1;  // OR_Gate or_5, 16 bits wide
  Multiplexer #(.width(16), .enable("false")) multiplexer_6 (.in0(or_5_out), .in1(not_3_out), .out(\output ), .sel(no));
  or or_6 (or_6_out, \output [0], \output [1], \output [2], \output [3], \output [4], \output [5], \output [6], \output [7], \output [8], \output [9], \output [10], \output [11], \output [12], \output [13], \output [14], \output [15]);
  Multiplexer #(.enable("false")) multiplexer_7 (.in0(1'b1), .in1(1'b0), .out(zr), .sel(or_6_out));
  Multiplexer #(.enable("false")) multiplexer_8 (.in0(1'b0), .in1(1'b1), .out(ng), .sel(\output [15]));
  // also tied to GND on the sheet: adder_1_cout

  // Notes on the sheet:
  //   x[i]
  //   y[i]
  //   ADDER
endmodule
