// Logisim project mux16.circ as structural Verilog: 1 circuit, main circuit main
module main (
  input  in_1,
  input  [15:0] in_2,
  input  [15:0] in_3,
  output [15:0] out_4
);

  wire and_1_out, and_2_out, and_3_out, and_4_out, and_5_out, and_6_out, and_7_out, and_8_out, and_9_out,
       and_10_out, and_11_out, and_12_out, and_13_out, and_14_out, and_15_out, and_16_out, and_17_out,
       and_18_out, and_19_out, and_20_out, and_21_out, and_22_out, and_23_out, and_24_out, and_25_out,
       and_26_out, and_27_out, and_28_out, and_29_out, and_30_out, and_31_out, and_32_out, not_1_out;

  not not_1 (not_1_out, in_1);
  and and_1 (and_1_out, not_1_out, in_2[0]);
  and and_2 (and_2_out, not_1_out, in_2[1]);
  and and_3 (and_3_out, not_1_out, in_2[2]);
  and and_4 (and_4_out, not_1_out, in_2[3]);
  and and_5 (and_5_out, not_1_out, in_2[4]);
  and and_6 (and_6_out, not_1_out, in_2[5]);
  and and_7 (and_7_out, not_1_out, in_2[6]);
  and and_8 (and_8_out, not_1_out, in_2[7]);
  and and_9 (and_9_out, not_1_out, in_2[8]);
  and and_10 (and_10_out, not_1_out, in_2[9]);
  and and_11 (and_11_out, not_1_out, in_2[10]);
  and and_12 (and_12_out, not_1_out, in_2[11]);
  and and_13 (and_13_out, not_1_out, in_2[12]);
  and and_14 (and_14_out, not_1_out, in_2[13]);
  and and_15 (and_15_out, not_1_out, in_2[14]);
  and and_16 (and_16_out, not_1_out, in_2[15]);
  and and_17 (and_17_out, in_1, in_3[0]);
  and and_18 (and_18_out, in_1, in_3[1]);
  and and_19 (and_19_out, in_1, in_3[2]);
  and and_20 (and_20_out, in_1, in_3[3]);
  and and_21 (and_21_out, in_1, in_3[4]);
  and and_22 (and_22_out, in_1, in_3[5]);
  and and_23 (and_23_out, in_1, in_3[6]);
  and and_24 (and_24_out, in_1, in_3[7]);
  and and_25 (and_25_out, in_1, in_3[8]);
  and and_26 (and_26_out, in_1, in_3[9]);
  and and_27 (and_27_out, in_1, in_3[10]);
  and and_28 (and_28_out, in_1, in_3[11]);
  and and_29 (and_29_out, in_1, in_3[12]);
  and and_30 (and_30_out, in_1, in_3[13]);
  and and_31 (and_31_out, in_1, in_3[14]);
  and and_32 (and_32_out, in_1, in_3[15]);
  or or_1 (out_4[0], and_1_out, and_17_out);
  or or_2 (out_4[1], and_2_out, and_18_out);
  or or_3 (out_4[2], and_3_out, and_19_out);
  or or_4 (out_4[3], and_4_out, and_20_out);
  or or_5 (out_4[4], and_5_out, and_21_out);
  or or_6 (out_4[5], and_6_out, and_22_out);
  or or_7 (out_4[6], and_7_out, and_23_out);
  or or_8 (out_4[7], and_8_out, and_24_out);
  or or_9 (out_4[8], and_9_out, and_25_out);
  or or_10 (out_4[9], and_10_out, and_26_out);
  or or_11 (out_4[10], and_11_out, and_27_out);
  or or_12 (out_4[11], and_12_out, and_28_out);
  or or_13 (out_4[12], and_13_out, and_29_out);
  or or_14 (out_4[13], and_14_out, and_30_out);
  or or_15 (out_4[14], and_15_out, and_31_out);
  or or_16 (out_4[15], and_16_out, and_32_out);
endmodule
