// Logisim project ALU_cricuits.circ as structural Verilog: 1 circuit, main circuit main
module main (
  input  [15:0] in_1,
  input  zx,
  input  nx,
  input  zy,
  input  ny,
  input  f,
  input  no,
  input  [15:0] x_i,
  input  [15:0] y_i,
  output [15:0] out_10,
  output [15:0] \output ,
  output [15:0] out_12
);

  wire adder_1_cout;
  wire [15:0] adder_1_out, and_1_out, and_2_out, and_3_out, multiplexer_1_out, multiplexer_2_out,
       multiplexer_5_out, not_1_out, not_2_out, not_3_out, or_1_out, or_2_out, or_3_out, or_4_out, or_5_out;

  assign or_1_out = x_i | in_1;  // OR_Gate or_1, 16 bits wide
  Multiplexer #(.width(16), .enable("false")) multiplexer_1 (
    .in0(or_1_out), .in1(and_1_out), .out(multiplexer_1_out), .sel(zx));
  assign and_1_out = x_i & in_1;  // AND_Gate and_1, 16 bits wide
  assign or_2_out = y_i | in_1;  // OR_Gate or_2, 16 bits wide
  assign and_2_out = y_i & in_1;  // AND_Gate and_2, 16 bits wide
  assign or_3_out = multiplexer_1_out | in_1;  // OR_Gate or_3, 16 bits wide
  assign not_1_out = ~multiplexer_1_out;  // NOT_Gate not_1, 16 bits wide
  Multiplexer #(.width(16), .enable("false")) multiplexer_2 (
    .in0(or_2_out), .in1(and_2_out), .out(multiplexer_2_out), .sel(zy));
  assign not_2_out = ~multiplexer_2_out;  // NOT_Gate not_2, 16 bits wide
  Multiplexer #(.width(16), .enable("false")) multiplexer_3 (.in0(or_3_out), .in1(not_1_out), .out(out_10), .sel(nx));
  assign or_4_out = multiplexer_2_out | in_1;  // OR_Gate or_4, 16 bits wide
  Multiplexer #(.width(16), .enable("false")) multiplexer_4 (.in0(or_4_out), .in1(not_2_out), .out(out_12), .sel(ny));
  assign and_3_out = out_10 & out_12;  // AND_Gate and_3, 16 bits wide
  Adder #(.width(16)) adder_1 (.a(out_10), .b(out_12), .out(adder_1_out), .cout(adder_1_cout));  // open: cin
  Multiplexer #(.width(16), .enable("false")) multiplexer_5 (
    .in0(and_3_out), .in1(adder_1_out), .out(multiplexer_5_out), .sel(f));
  assign not_3_out = ~multiplexer_5_out;  // NOT_Gate not_3, 16 bits wide
  assign or_5_out = multiplexer_5_out | in_1;  // OR_Gate or_5, 16 bits wide
  Multiplexer #(.width(16), .enable("false")) multiplexer_6 (.in0(or_5_out), .in1(not_3_out), .out(\output ), .sel(no));
  // also tied to GND on the sheet: adder_1_cout

  // Notes on the sheet:
  //   x[i]
  //   y[i]
  //   ADDER
endmodule
