// Logisim project Model1.circ as structural Verilog: 1 circuit, main circuit main
module main (
  input  [15:0] in_1,
  output [15:0] out_2,
  output [15:0] out_3,
  output [15:0] out_4,
  output zx,
  output nx,
  output zy,
  output ny,
  output f,
  output no,
  output zr,
  output [15:0] out_12,
  output [15:0] x_input,
  output [15:0] _3__Data_Bus,
  output [15:0] out_15,
  output [15:0] out_16,
  output [15:0] out_17,
  output [15:0] y_input,
  output [15:0] out_19,
  output [15:0] out_20,
  output [15:0] \output ,
  output [15:0] out_22,
  output ng,
  output [5:0] out_24,
  output [5:0] out_25,
  output [15:0] addresss
);

  wire and_1_out, and_4_out, and_5_out, and_6_out, and_8_out, and_9_out, and_10_out, and_11_out,
       button_2_out, button_3_out, button_4_out, clock_1_out, clock_2_out, comparator_1_eq, comparator_2_eq,
       comparator_2_gt, comparator_3_eq, comparator_3_lt, digital_oscilloscope_1_p4, keyboard_1_avail,
       multiplexer_13_out, not_1_out, not_2_out, not_3_out, not_7_out, not_8_out, or_1_out, or_6_out,
       or_8_out, or_9_out, or_10_out, or_11_out, or_13_out, rgb_video_1_p1;
  wire [6:0] keyboard_1_data;
  wire [14:0] bitselector_3_out, multiplexer_12_out;
  wire [15:0] adder_1_out, adder_2_out, and_2_out, and_3_out, and_7_out, divider_1_out, divider_2_rem,
       multiplexer_1_out, multiplexer_3_out, multiplexer_4_out, multiplexer_7_out, multiplexer_9_out,
       multiplexer_14_out, not_4_out, not_5_out, not_6_out, or_2_out, or_3_out, or_4_out, or_5_out, or_7_out,
       subtractor_1_out, subtractor_2_out;

  Clock clock_1 (.out(clock_1_out));
  // Digital_Oscilloscope #(.nState(7)) digital_oscilloscope_1: pin names not known; wires that end beside it: clock_1_out, clock_1_out, 1'b1, digital_oscilloscope_1_p4
  ROM #(.addrWidth(15), .dataWidth(16)) rom_1 (
    .addr(addresss[14:0]), .data({out_3[15:11], nx, out_3[9], ny, f, no, out_3[5:0]}));
  Button button_1 (.out(digital_oscilloscope_1_p4));
  Hex_Digit_Display #(.decimalPoint("false")) hex_digit_display_1 (.value(out_3[15:12]));
  // LedBar #(.inputtype("row"), .matrixcols(16)) ledbar_1: pin names not known; wires that end beside it: {out_3[15:11], nx, out_3[9], ny, f, no, out_3[5:0]}, out_3[15], out_3[14], out_3[13], out_3[12], out_3[5], out_3[4], out_3[3], out_3[2], out_3[1], out_3[0]
  Hex_Digit_Display #(.decimalPoint("false")) hex_digit_display_2 (.value({out_3[11], nx, out_3[9], ny}));
  Hex_Digit_Display #(.decimalPoint("false")) hex_digit_display_3 (.value({f, no, out_3[5:4]}));
  Hex_Digit_Display #(.decimalPoint("false")) hex_digit_display_4 (.value(out_3[3:0]));
  Multiplexer #(.width(16)) multiplexer_1 (
    .in0({out_3[15:11], nx, out_3[9], ny, f, no, out_3[5:0]}), .in1(out_16), .out(multiplexer_1_out),
    .sel(out_3[15]));
  not not_1 (not_1_out, out_3[15]);
  Register #(.trigger("falling"), .width(16)) AddressRegister (
    .D(multiplexer_1_out), .en(or_1_out), .clk(clock_1_out), .Q(out_2), .clr(digital_oscilloscope_1_p4));
  or or_1 (or_1_out, out_3[5], not_1_out);
  Register #(.trigger("falling"), .width(16)) DataRegister (
    .D(out_16), .en(and_1_out), .clk(clock_1_out), .Q(out_4), .clr(digital_oscilloscope_1_p4));
  and and_1 (and_1_out, out_3[15], out_3[4]);
  Multiplexer #(.width(16)) multiplexer_2 (.in0(out_2), .in1(_3__Data_Bus), .out(out_20), .sel(out_3[12]));
  not not_2 (not_2_out, zr);
  not not_3 (not_3_out, ng);
  assign or_2_out = out_4 | in_1;  // OR_Gate or_2, 16 bits wide
  assign and_2_out = out_4 & in_1;  // AND_Gate and_2, 16 bits wide
  assign or_3_out = out_20 | in_1;  // OR_Gate or_3, 16 bits wide
  assign and_3_out = out_20 & in_1;  // AND_Gate and_3, 16 bits wide
  and and_4 (and_4_out, out_3[2], ng);
  and and_5 (and_5_out, out_3[1], zr);
  and and_6 (and_6_out, out_3[0], not_2_out, not_3_out);
  Multiplexer #(.width(16)) multiplexer_3 (.in0(or_2_out), .in1(and_2_out), .out(multiplexer_3_out), .sel(out_3[11]));
  assign not_4_out = ~multiplexer_3_out;  // NOT_Gate not_4, 16 bits wide
  Multiplexer #(.width(16)) multiplexer_4 (.in0(or_3_out), .in1(and_3_out), .out(multiplexer_4_out), .sel(out_3[9]));
  assign not_5_out = ~multiplexer_4_out;  // NOT_Gate not_5, 16 bits wide
  assign or_4_out = multiplexer_3_out | in_1;  // OR_Gate or_4, 16 bits wide
  Multiplexer #(.width(16)) multiplexer_5 (.in0(or_4_out), .in1(not_4_out), .out(out_17), .sel(nx));
  assign or_5_out = multiplexer_4_out | in_1;  // OR_Gate or_5, 16 bits wide
  Multiplexer #(.width(16)) multiplexer_6 (.in0(or_5_out), .in1(not_5_out), .out(out_22), .sel(ny));
  or or_6 (or_6_out, and_4_out, and_5_out, and_6_out);
  assign and_7_out = out_17 & out_22;  // AND_Gate and_7, 16 bits wide
  Adder #(.width(16)) adder_1 (.a(out_17), .b(out_22), .out(adder_1_out));  // open: cin, cout
  Multiplexer #(.width(16)) multiplexer_7 (.in0(and_7_out), .in1(adder_1_out), .out(multiplexer_7_out), .sel(f));
  assign not_6_out = ~multiplexer_7_out;  // NOT_Gate not_6, 16 bits wide
  assign or_7_out = multiplexer_7_out | in_1;  // OR_Gate or_7, 16 bits wide
  Multiplexer #(.width(16)) multiplexer_8 (.in0(or_7_out), .in1(not_6_out), .out(out_16), .sel(no));
  and and_8 (and_8_out, or_6_out, out_3[15]);
  Button button_2 (.out(button_2_out));
  or or_8 (or_8_out, out_16[0], out_16[1], out_16[2], out_16[3], out_16[4], out_16[5], out_16[6], out_16[7], out_16[8], out_16[9], out_16[10], out_16[11], out_16[12], out_16[13], out_16[14], out_16[15]);
  Multiplexer #(.width(16)) multiplexer_9 (.in0(adder_2_out), .in1(out_2), .out(multiplexer_9_out), .sel(and_8_out));
  Multiplexer multiplexer_10 (.in0(1'b1), .in1(1'b0), .out(zr), .sel(or_8_out));
  Multiplexer multiplexer_11 (.in0(1'b0), .in1(1'b1), .out(ng), .sel(out_16[15]));
  Register #(.trigger("falling"), .width(16)) register_1 (
    .D(multiplexer_9_out), .en(1'b1), .clk(clock_1_out), .Q(addresss), .clr(or_9_out));
  or or_9 (or_9_out, button_2_out, digital_oscilloscope_1_p4);
  Clock clock_2 (.out(clock_2_out));
  Hex_Digit_Display #(.decimalPoint("false")) hex_digit_display_5 (.value(addresss[15:12]));
  Hex_Digit_Display #(.decimalPoint("false")) hex_digit_display_6 (.value(addresss[11:8]));
  Hex_Digit_Display #(.decimalPoint("false")) hex_digit_display_7 (.value(addresss[7:4]));
  and and_9 (and_9_out, out_3[15], out_3[3]);
  Hex_Digit_Display #(.decimalPoint("false")) hex_digit_display_8 (.value(addresss[3:0]));
  Adder #(.width(16)) adder_2 (.a(addresss), .b(16'h1), .out(adder_2_out));  // open: cin, cout
  Comparator #(.mode("unsigned"), .width(16)) comparator_1 (
    .a({out_3[15:11], nx, out_3[9], ny, f, no, out_3[5:0]}), .b(16'h5001), .eq(comparator_1_eq));  // open: gt, lt
  RAM #(.addrWidth(15), .clearpin("true"), .dataWidth(16), .enables("line"), .trigger("falling"), .\type ("nonvolatile")) ram_1 (
    .addr(multiplexer_12_out), .we(multiplexer_13_out), .oe(1'b1), .clk(clock_1_out),
    .din(multiplexer_14_out), .dout(_3__Data_Bus), .clr(digital_oscilloscope_1_p4));
  Subtractor #(.width(16)) subtractor_1 (.a(out_2), .b(16'h4000), .out(subtractor_1_out));  // open: bin, bout
  Multiplexer #(.width(15)) multiplexer_12 (
    .in0(out_2[14:0]), .in1(15'h5001), .out(multiplexer_12_out), .sel(comparator_1_eq));
  Subtractor #(.width(16)) subtractor_2 (.a(out_2), .b(16'h4000), .out(subtractor_2_out));  // open: bin, bout
  or or_10 (or_10_out, comparator_2_gt, comparator_2_eq);
  Comparator #(.mode("unsigned"), .width(16)) comparator_2 (
    .a(subtractor_1_out), .b({16{1'b0}}), .gt(comparator_2_gt), .eq(comparator_2_eq));  // open: lt
  or or_11 (or_11_out, comparator_3_eq, comparator_3_lt);
  Comparator #(.mode("unsigned"), .width(16)) comparator_3 (
    .a(subtractor_1_out), .b(16'h1000), .eq(comparator_3_eq), .lt(comparator_3_lt));  // open: gt
  Multiplexer multiplexer_13 (.in0(and_9_out), .in1(1'b1), .out(multiplexer_13_out), .sel(comparator_1_eq));
  Divider #(.width(16)) divider_1 (.a(subtractor_2_out), .b(16'h40), .out(divider_1_out));  // open: upper, rem
  Divider #(.width(16)) divider_2 (.a(subtractor_2_out), .b(16'h40), .rem(divider_2_rem));  // open: out, upper
  BitSelector #(.group(6), .width(16)) bitselector_1 (.in(divider_1_out), .out(out_25), .sel(2'b00));
  and and_10 (and_10_out, or_10_out, or_11_out);
  Button button_3 (.out(button_3_out));
  Button button_4 (.out(button_4_out));
  Multiplexer #(.width(16)) multiplexer_14 (
    .in0(out_16), .in1({{9{1'b0}}, keyboard_1_data}), .out(multiplexer_14_out), .sel(comparator_1_eq));
  BitSelector #(.group(6), .width(16)) bitselector_2 (.in(divider_2_rem), .out(out_24), .sel(2'b00));
  BitSelector #(.group(15), .width(16)) bitselector_3 (.in(out_16), .out(bitselector_3_out), .sel(1'b0));
  and and_11 (and_11_out, and_10_out, and_9_out);
  not not_7 (not_7_out, clock_1_out);
  // RGB_Video #(.height(64), .scale(8), .width(64)) rgb_video_1: pin names not known; wires that end beside it: rgb_video_1_p1, not_7_out, and_11_out, out_24, out_25, bitselector_3_out
  or or_12 (rgb_video_1_p1, button_3_out, digital_oscilloscope_1_p4);
  not not_8 (not_8_out, not_7_out);
  or or_13 (or_13_out, button_4_out, digital_oscilloscope_1_p4);
  Keyboard #(.buflen(5), .trigger("falling")) keyboard_1 (
    .clk(not_8_out), .re(comparator_1_eq), .clr(or_13_out), .avail(keyboard_1_avail), .data(keyboard_1_data));
  LED led_1 (.in(keyboard_1_avail));

  assign {out_3[10], out_3[8:6]} = {nx, ny, f, no};
  assign out_12 = out_2;
  assign out_15 = out_4;
  assign out_19 = out_16;
  assign \output  = out_16;
  assign x_input = out_4;
  assign y_input = out_20;
  assign zx = out_3[11];
  assign zy = out_3[9];

  // Notes on the sheet:
  //   contents of rom_1 (hex, n*v repeats v):
  //   3da1 ec10 404b e308 405d e308 4087 e308 4088 e308 4092 e308 409a e308 409f e308 40a3 e308 40a4 e308
  //   40ad e308 40b0 e308 40cd e308 4174 e308 4182 e308 41ef e308 4200 e308 42b7 e308 4372 e308 43b2 e308
  //   43f2 e308 4433 e308 4439 e308 4477 e308 4479 e308 5af ec10 407c e308 423d e308 4255 e308 425b e308
  //   427d e308 4289 e308 4301 e308 431f e308 43ca e308 43d2 e308 440a e308 4429 e308 447f e308 4498 e308
  //   44a0 e308 44bc e308 44ec e308 4526 e308 452d e308 456a e308 45ad e308 45b4 e308 45e9 e308 45f6 e308
  //   45f9 e308 4617 e308 4620 e308 466f e308 46d0 e308 46d1 e308 46e2 e308 46eb e308 46fe e308 4750 e308
  //   475e e308 47b2 e308 47d4 e308 4897 e308 48d9 e308 49ce e308 49fa e308 4a12 e308 4acb e308 4aff e308
  //   4b0c e308 4b3f e308 19e1 ec10 40bf e308 413a e308 413b e308 4365 e308 4366 e308 43ef e308 4411 e308
  //   4412 e308 4415 e308 4455 e308 445f e308 44a4 e308 44e9 e308 45f0 e308 4623 e308 4631 e308 4670 e308
  //   4685 e308 4689 e308 469b e308 47a2 e308 4815 e308 48a2 e308 4962 e308 49a2 e308 49e2 e308 4a61 e308
  //   4a9e e308 4ae1 e308 4b20 e308 4b60 e308 35f ec10 4263 e308 4264 e308 42e6 e308 435d e308 435e e308
  //   4389 e308 439c e308 4457 e308 4491 e308 4499 e308 44d9 e308 4511 e308 451b e308 455b e308 4597 e308
  //   45cb e308 45d8 e308 45dc e308 4603 e308 4619 e308 462c e308 4659 e308 469e e308 46c4 e308 472d e308
  //   4794 e308 479f e308 47df e308 481c e308 48a4 e308 48ea e308 48ec e308 491d e308 49e0 e308 4a99 e308
  //   4b24 e308 4cd5 e308 4d42 e308 4ed3 e308 4f0b e308 4f53 e308 4f90 e308 4f92 e308 7c00 ec10 4565 e308
  //   4566 e308 45e3 e308 481d e308 499d e308 49da e308 49dd e308 4a1d e308 4a59 e308 4a98 e308 4b5c e308
  //   4c17 e308 4c59 e308 4c96 e308 4cd7 e308 5e1 ec10 466d e308 466e e308 46ab e308 46ae e308 4761 e308
  //   47ac e308 482c e308 4855 e308 48ac e308 48ad e308 4923 e308 492e e308 4961 e308 4a11 e308 4a15 e308
  //   4a51 e308 4a86 e308 4a8a e308 4ac7 e308 4ad3 e308 4ae5 e308 4b30 e308 4b65 e308 4b8f e308 4b99 e308
  //   4b9b e308 4ba3 e308 4bb0 e308 4c1c e308 4d30 e308 4de7 e308 4df0 e308 4e2c e308 4e2e e308 4e2f e308
  //   5c72 ec10 4b78 e308 4bb6 e308 4bb7 e308 4c33 e308 4c71 e308 4cee e308 4d2d e308 4d6d e308 4dae e308
  //   4daf e308 4dc0 e308 4dda e308 4de6 e308 4dea e308 4def e308 4eca e308 4ef1 e308 4fdf e308 1b6 ea87
  //   CPU
  //   CLOCK
  //   ROM 64KB
  //   RESET
  //   MSB
  //   Hexadecimal format
  //   111accccccdddjjj
  //   0vvvvvvvvvvvvvvv
  //   addresss
  //   Instruction
  //   LSB
  //   1st
  //   2) Control Bus Lines
  //   inM
  //   ALU output
  //   2nd
  //   address
  //   inM
  //   ALU input
  //   Zero Constant
  //   D
  //   A/M
  //   x[i]
  //   y[i]
  //   ALU output
  //   ALU
  //   J
  //   3) Data Bus
  //   1) Address Bus
  //   ADDER
  //   jumpFlag
  //   Address Register
  //   ALU output
  //   ALU output
  //   Reset Button
  //   PROGRAM COUNTER
  //   Flags
  //   write
  //   read
  //   MSB Line
  //   Hexadecimal format
  //   20,481
  //   Instruction addresss
  //   RAM 64KB
  //   ALU output
  //   HARVARD ARCHITECTURE
  //   Enable KBD
  //   Enable KBD
  //   20,481
  //   Input Line
  //   X
  //   Y coordinate
  //   Y
  //   )
  //   Keyboard Reset
  //   Keyboard Line
  //   X coordinate
  //   Screen Reset
  //   ALU output
  //   COMPUTER
  //   Display
  //   Keyboard Line
  //   Keyboard 
  //   Qwerty
endmodule
