// Logisim project CPU.circ as structural Verilog: 1 circuit, main circuit main
module main (
  input  [15:0] in_1,
  output [15:0] out_2,
  output [15:0] out_3,
  output [15:0] out_4,
  output zx,
  output nx,
  output zy,
  output ny,
  output f,
  output no,
  output zr,
  output [15:0] out_12,
  output [15:0] x_input,
  output [15:0] _3__Data_Bus,
  output [15:0] out_15,
  output [15:0] out_16,
  output [15:0] out_17,
  output [15:0] y_input,
  output [15:0] out_19,
  output [15:0] out_20,
  output [15:0] \output ,
  output [15:0] out_22,
  output ng,
  output [15:0] addresss
);

  wire and_1_out, and_4_out, and_5_out, and_6_out, and_8_out, and_9_out, button_2_out, clock_1_out,
       clock_2_out, digital_oscilloscope_1_p4, not_1_out, not_2_out, not_3_out, or_1_out, or_6_out, or_8_out,
       or_9_out;
  wire [15:0] adder_1_out, adder_2_out, and_2_out, and_3_out, and_7_out, multiplexer_1_out,
       multiplexer_3_out, multiplexer_4_out, multiplexer_7_out, multiplexer_9_out, not_4_out, not_5_out,
       not_6_out, or_2_out, or_3_out, or_4_out, or_5_out, or_7_out;

  Clock clock_1 (.out(clock_1_out));
  // Digital_Oscilloscope #(.nState(7)) digital_oscilloscope_1: pin names not known; wires that end beside it: clock_1_out, clock_1_out, 1'b1, digital_oscilloscope_1_p4
  ROM #(.addrWidth(15), .dataWidth(16)) rom_1 (
    .addr(addresss[14:0]), .data({out_3[15:11], nx, out_3[9], ny, f, no, out_3[5:0]}));
  Button button_1 (.out(digital_oscilloscope_1_p4));
  Hex_Digit_Display #(.decimalPoint("false")) hex_digit_display_1 (.value(out_3[15:12]));
  // LedBar #(.inputtype("row"), .matrixcols(16)) ledbar_1: pin names not known; wires that end beside it: {out_3[15:11], nx, out_3[9], ny, f, no, out_3[5:0]}, out_3[15], out_3[14], out_3[13], out_3[12], out_3[5], out_3[4], out_3[3], out_3[2], out_3[1], out_3[0]
  Hex_Digit_Display #(.decimalPoint("false")) hex_digit_display_2 (.value({out_3[11], nx, out_3[9], ny}));
  Hex_Digit_Display #(.decimalPoint("false")) hex_digit_display_3 (.value({f, no, out_3[5:4]}));
  Hex_Digit_Display #(.decimalPoint("false")) hex_digit_display_4 (.value(out_3[3:0]));
  Multiplexer #(.width(16)) multiplexer_1 (
    .in0({out_3[15:11], nx, out_3[9], ny, f, no, out_3[5:0]}), .in1(out_16), .out(multiplexer_1_out),
    .sel(out_3[15]));
  not not_1 (not_1_out, out_3[15]);
  Register #(.trigger("falling"), .width(16)) AddressRegister (
    .D(multiplexer_1_out), .en(or_1_out), .clk(clock_1_out), .Q(out_2), .clr(digital_oscilloscope_1_p4));
  or or_1 (or_1_out, out_3[5], not_1_out);
  Register #(.trigger("falling"), .width(16)) DataRegister (
    .D(out_16), .en(and_1_out), .clk(clock_1_out), .Q(out_4), .clr(digital_oscilloscope_1_p4));
  and and_1 (and_1_out, out_3[15], out_3[4]);
  Multiplexer #(.width(16)) multiplexer_2 (.in0(out_2), .in1(_3__Data_Bus), .out(out_20), .sel(out_3[12]));
  not not_2 (not_2_out, zr);
  not not_3 (not_3_out, ng);
  assign or_2_out = out_4 | in_1;  // OR_Gate or_2, 16 bits wide
  assign and_2_out = out_4 & in_1;  // AND_Gate and_2, 16 bits wide
  assign or_3_out = out_20 | in_1;  // OR_Gate or_3, 16 bits wide
  assign and_3_out = out_20 & in_1;  // AND_Gate and_3, 16 bits wide
  and and_4 (and_4_out, out_3[2], ng);
  and and_5 (and_5_out, out_3[1], zr);
  and and_6 (and_6_out, out_3[0], not_2_out, not_3_out);
  Multiplexer #(.width(16)) multiplexer_3 (.in0(or_2_out), .in1(and_2_out), .out(multiplexer_3_out), .sel(out_3[11]));
  assign not_4_out = ~multiplexer_3_out;  // NOT_Gate not_4, 16 bits wide
  Multiplexer #(.width(16)) multiplexer_4 (.in0(or_3_out), .in1(and_3_out), .out(multiplexer_4_out), .sel(out_3[9]));
  assign not_5_out = ~multiplexer_4_out;  // NOT_Gate not_5, 16 bits wide
  assign or_4_out = multiplexer_3_out | in_1;  // OR_Gate or_4, 16 bits wide
  Multiplexer #(.width(16)) multiplexer_5 (.in0(or_4_out), .in1(not_4_out), .out(out_17), .sel(nx));
  assign or_5_out = multiplexer_4_out | in_1;  // OR_Gate or_5, 16 bits wide
  Multiplexer #(.width(16)) multiplexer_6 (.in0(or_5_out), .in1(not_5_out), .out(out_22), .sel(ny));
  or or_6 (or_6_out, and_4_out, and_5_out, and_6_out);
  assign and_7_out = out_17 & out_22;  // AND_Gate and_7, 16 bits wide
  Adder #(.width(16)) adder_1 (.a(out_17), .b(out_22), .out(adder_1_out));  // open: cin, cout
  Multiplexer #(.width(16)) multiplexer_7 (.in0(and_7_out), .in1(adder_1_out), .out(multiplexer_7_out), .sel(f));
  assign not_6_out = ~multiplexer_7_out;  // NOT_Gate not_6, 16 bits wide
  assign or_7_out = multiplexer_7_out | in_1;  // OR_Gate or_7, 16 bits wide
  Multiplexer #(.width(16)) multiplexer_8 (.in0(or_7_out), .in1(not_6_out), .out(out_16), .sel(no));
  and and_8 (and_8_out, or_6_out, out_3[15]);
  Button button_2 (.out(button_2_out));
  or or_8 (or_8_out, out_16[0], out_16[1], out_16[2], out_16[3], out_16[4], out_16[5], out_16[6], out_16[7], out_16[8], out_16[9], out_16[10], out_16[11], out_16[12], out_16[13], out_16[14], out_16[15]);
  Multiplexer #(.width(16)) multiplexer_9 (.in0(adder_2_out), .in1(out_2), .out(multiplexer_9_out), .sel(and_8_out));
  Multiplexer multiplexer_10 (.in0(1'b1), .in1(1'b0), .out(zr), .sel(or_8_out));
  Multiplexer multiplexer_11 (.in0(1'b0), .in1(1'b1), .out(ng), .sel(out_16[15]));
  Register #(.trigger("falling"), .width(16)) register_1 (
    .D(multiplexer_9_out), .en(1'b1), .clk(clock_1_out), .Q(addresss), .clr(or_9_out));
  or or_9 (or_9_out, button_2_out, digital_oscilloscope_1_p4);
  Clock clock_2 (.out(clock_2_out));
  Hex_Digit_Display #(.decimalPoint("false")) hex_digit_display_5 (.value(addresss[15:12]));
  Hex_Digit_Display #(.decimalPoint("false")) hex_digit_display_6 (.value(addresss[11:8]));
  Hex_Digit_Display #(.decimalPoint("false")) hex_digit_display_7 (.value(addresss[7:4]));
  and and_9 (and_9_out, out_3[15], out_3[3]);
  Hex_Digit_Display #(.decimalPoint("false")) hex_digit_display_8 (.value(addresss[3:0]));
  Adder #(.width(16)) adder_2 (.a(addresss), .b(16'h1), .out(adder_2_out));  // open: cin, cout
  RAM #(.addrWidth(15), .clearpin("true"), .dataWidth(16), .enables("line"), .trigger("falling"), .\type ("nonvolatile")) ram_1 (
    .addr(out_2[14:0]), .we(and_9_out), .oe(1'b1), .clk(clock_1_out), .din(out_16), .dout(_3__Data_Bus),
    .clr(digital_oscilloscope_1_p4));

  assign {out_3[10], out_3[8:6]} = {nx, ny, f, no};
  assign out_12 = out_2;
  assign out_15 = out_4;
  assign out_19 = out_16;
  assign \output  = out_16;
  assign x_input = out_4;
  assign y_input = out_20;
  assign zx = out_3[11];
  assign zy = out_3[9];

  // Notes on the sheet:
  //   contents of rom_1 (hex, n*v repeats v):
  //   0 ec10 10 e308 1 ec10 11 e308 3 ec10 12 e308 13 efc8 14 14 ec10 15 e308 c8 ea88 c9 efc8 ca ec10 0
  //   e308 15 fc10 12 f1d0 3a e302 11 fc10 14 e308 10 fc10 11 f088 14 fc10 10 e308 11 fc10 13 f088 0 fc20
  //   e308 0 fdc8 12 fdc8 1b ea87 13 fc10 0 fc20 e308 3f ea87
  //   CPU
  //   CLOCK
  //   ROM 64KB
  //   RESET
  //   MSB
  //   Hexadecimal format
  //   111accccccdddjjj
  //   0vvvvvvvvvvvvvvv
  //   addresss
  //   Instruction
  //   LSB
  //   1st
  //   2) Control Bus Lines
  //   inM
  //   ALU output
  //   2nd
  //   address
  //   inM
  //   ALU input
  //   Zero Constant
  //   D
  //   A/M
  //   x[i]
  //   y[i]
  //   ALU output
  //   ALU
  //   J
  //   3) Data Bus
  //   1) Address Bus
  //   ADDER
  //   jumpFlag
  //   Address Register
  //   ALU output
  //   ALU output
  //   Reset Button
  //   PROGRAM COUNTER
  //   Flags
  //   write
  //   read
  //   MSB Line
  //   Hexadecimal format
  //   Instruction addresss
  //   RAM 64KB
endmodule
