// Logisim project 8RAM.circ as structural Verilog: 1 circuit, main circuit main
module main (
  input  in_1,
  input  [15:0] inpuut,
  input  load,
  input  [2:0] adddress
);

  wire clock_1_out, demultiplexer_1_out0, demultiplexer_1_out1, demultiplexer_1_out2, demultiplexer_1_out3,
       demultiplexer_1_out4, demultiplexer_1_out5, demultiplexer_1_out6, demultiplexer_1_out7;
  wire [15:0] demultiplexer_2_out0, demultiplexer_2_out1, demultiplexer_2_out2, demultiplexer_2_out3,
       demultiplexer_2_out4, demultiplexer_2_out5, demultiplexer_2_out6, demultiplexer_2_out7,
       multiplexer_1_out, register_1_q, register_2_q, register_3_q, register_4_q, register_5_q, register_6_q,
       register_7_q, register_8_q;

  LedBar #(.matrixcols(16)) ledbar_1 (
    .led0(inpuut[15]), .led1(inpuut[14]), .led2(inpuut[13]), .led3(inpuut[12]), .led4(inpuut[11]),
    .led5(inpuut[10]), .led6(inpuut[9]), .led7(inpuut[8]), .led8(inpuut[7]), .led9(inpuut[6]),
    .led10(inpuut[5]), .led11(inpuut[4]), .led12(inpuut[3]), .led13(inpuut[2]), .led14(inpuut[1]),
    .led15(inpuut[0]));
  Demultiplexer #(.select(3)) demultiplexer_1 (
    .out0(demultiplexer_1_out0), .out1(demultiplexer_1_out1), .out2(demultiplexer_1_out2),
    .out3(demultiplexer_1_out3), .out4(demultiplexer_1_out4), .out5(demultiplexer_1_out5),
    .out6(demultiplexer_1_out6), .out7(demultiplexer_1_out7), .in(load), .sel(adddress));
  Demultiplexer #(.select(3), .width(16)) demultiplexer_2 (
    .out0(demultiplexer_2_out0), .out1(demultiplexer_2_out1), .out2(demultiplexer_2_out2),
    .out3(demultiplexer_2_out3), .out4(demultiplexer_2_out4), .out5(demultiplexer_2_out5),
    .out6(demultiplexer_2_out6), .out7(demultiplexer_2_out7), .in(inpuut), .sel(adddress));
  Clock clock_1 (.out(clock_1_out));
  LED led_1 (.in(clock_1_out));
  Register #(.trigger("falling"), .width(16)) register_1 (
    .D(demultiplexer_2_out0), .en(demultiplexer_1_out0), .clk(clock_1_out), .Q(register_1_q), .clr(in_1));
  Register #(.trigger("falling"), .width(16)) register_2 (
    .D(demultiplexer_2_out1), .en(demultiplexer_1_out1), .clk(clock_1_out), .Q(register_2_q), .clr(in_1));
  Register #(.trigger("falling"), .width(16)) register_3 (
    .D(demultiplexer_2_out2), .en(demultiplexer_1_out2), .clk(clock_1_out), .Q(register_3_q), .clr(in_1));
  Register #(.trigger("falling"), .width(16)) register_4 (
    .D(demultiplexer_2_out3), .en(demultiplexer_1_out3), .clk(clock_1_out), .Q(register_4_q), .clr(in_1));
  Register #(.trigger("falling"), .width(16)) register_5 (
    .D(demultiplexer_2_out4), .en(demultiplexer_1_out4), .clk(clock_1_out), .Q(register_5_q), .clr(in_1));
  Register #(.trigger("falling"), .width(16)) register_6 (
    .D(demultiplexer_2_out5), .en(demultiplexer_1_out5), .clk(clock_1_out), .Q(register_6_q), .clr(in_1));
  Register #(.trigger("falling"), .width(16)) register_7 (
    .D(demultiplexer_2_out6), .en(demultiplexer_1_out6), .clk(clock_1_out), .Q(register_7_q), .clr(in_1));
  Register #(.trigger("falling"), .width(16)) register_8 (
    .D(demultiplexer_2_out7), .en(demultiplexer_1_out7), .clk(clock_1_out), .Q(register_8_q), .clr(in_1));
  LedBar #(.matrixcols(16)) ledbar_2 (
    .led0(multiplexer_1_out[15]), .led1(multiplexer_1_out[14]), .led2(multiplexer_1_out[13]),
    .led3(multiplexer_1_out[12]), .led4(multiplexer_1_out[11]), .led5(multiplexer_1_out[10]),
    .led6(multiplexer_1_out[9]), .led7(multiplexer_1_out[8]), .led8(multiplexer_1_out[7]),
    .led9(multiplexer_1_out[6]), .led10(multiplexer_1_out[5]), .led11(multiplexer_1_out[4]),
    .led12(multiplexer_1_out[3]), .led13(multiplexer_1_out[2]), .led14(multiplexer_1_out[1]),
    .led15(multiplexer_1_out[0]));
  Multiplexer #(.select(3), .width(16)) multiplexer_1 (
    .in0(register_1_q), .in1(register_2_q), .in2(register_3_q), .in3(register_4_q), .in4(register_5_q),
    .in5(register_6_q), .in6(register_7_q), .in7(register_8_q), .out(multiplexer_1_out), .sel(adddress));
  // Digital_Oscilloscope #(.frontlines("falling")) OSCILLOSCOPE: pin names not known; wires that end beside it: clock_1_out, load
  Hex_Digit_Display #(.decimalPoint("false")) locationn (.value({1'b0, adddress}));

  // Notes on the sheet:
  //   8RAM
  //   segmented display
endmodule
