// Logisim project RAM32kB.circ as structural Verilog: 1 circuit, main circuit main
module main (
  input  [13:0] adress,
  input  write,
  input  read,
  input  [15:0] inputt,
  output [15:0] display
);

  wire clock_1_out, reset_out;

  Button reset (.out(reset_out));
  Clock clock_1 (.out(clock_1_out));
  RAM #(.addrWidth(14), .clearpin("true"), .dataWidth(16), .trigger("falling"), .\type ("nonvolatile")) ram_1 (
    .addr(adress), .we(write), .oe(read), .clk(clock_1_out), .din(inputt), .dout(display), .clr(reset_out));
endmodule
