// Logisim project memory_fun.circ as structural Verilog: 1 circuit, main circuit main
module main (
  input  in_1,
  input  [3:0] in_2,
  input  in_3,
  input  in_4,
  input  [3:0] in_5,
  input  [6:0] in_6,
  input  [15:0] in_7,
  input  in_8,
  input  in_9,
  input  [15:0] in_10,
  input  in_11,
  input  in_12,
  input  in_13,
  input  in_14,
  input  PROGRAM_COUNTER,
  input  [1:0] in_16,
  input  in_17,
  input  [15:0] in_18,
  input  [15:0] in_19,
  input  [15:0] in_20,
  input  in_21,
  input  [1:0] in_22,
  input  [15:0] inpuut,
  input  load,
  input  [1:0] in_25,
  input  [15:0] in_26,
  input  [2:0] adddress,
  input  [2:0] ADDRESS,
  input  [13:0] adress,
  input  write,
  input  read,
  input  [15:0] inputt,
  output [15:0] out_33,
  output [15:0] out_34,
  output [15:0] addresss,
  output [15:0] out_36,
  output [15:0] outpput,
  output [15:0] display
);

  wire button_1_out, button_2_out, button_3_out, clock_1_out, clock_2_out, clock_3_out, clock_4_out,
       clock_5_out, clock_6_out, clock_7_out, demultiplexer_3_out0, demultiplexer_3_out1,
       demultiplexer_3_out2, demultiplexer_3_out3, demultiplexer_3_out4, demultiplexer_3_out5,
       demultiplexer_3_out6, demultiplexer_3_out7, not_1_out, reset_out;
  wire [1:0] counter_1_q_2;
  wire [11:0] counter_1_q;
  wire [15:0] adder_1_out, demultiplexer_1_out0, demultiplexer_1_out1, demultiplexer_1_out2,
       demultiplexer_1_out3, demultiplexer_1_out4, demultiplexer_1_out5, demultiplexer_1_out6,
       demultiplexer_1_out7, demultiplexer_2_out0, demultiplexer_4_out0, demultiplexer_4_out1,
       demultiplexer_4_out2, demultiplexer_4_out3, demultiplexer_4_out4, demultiplexer_4_out5,
       demultiplexer_4_out6, demultiplexer_4_out7, multiplexer_3_out, register_2_q, register_3_q,
       register_4_q, register_5_q, register_6_q, register_7_q, register_8_q, register_9_q,
       shift_register_2_p16, shift_register_2_p17, shift_register_2_p18, shift_register_2_p19,
       shift_register_2_p20, shift_register_2_p21, shift_register_2_p22, shift_register_2_p23;

  Clock clock_1 (.out(clock_1_out));
  LedBar #(.matrixcols(16)) ledbar_1 (
    .led0(in_26[15]), .led1(in_26[14]), .led2(in_26[13]), .led3(in_26[12]), .led4(in_26[11]),
    .led5(in_26[10]), .led6(in_26[9]), .led7(in_26[8]), .led8(in_26[7]), .led9(in_26[6]), .led10(in_26[5]),
    .led11(in_26[4]), .led12(in_26[3]), .led13(in_26[2]), .led14(in_26[1]), .led15(in_26[0]));
  Button button_1 (.out(button_1_out));
  Clock clock_2 (.out(clock_2_out));
  LED led_1 (.in(clock_2_out));
  Button reset (.out(reset_out));
  // Shift_Register #(.length(16), .trigger("falling")) shift_register_1: pin names not known; wires that end beside it: button_1_out, in_1, 1'b0, clock_1_out, in_10[0], in_10[1], in_10[2], in_10[3], in_10[4], in_10[5], in_10[6], in_10[7], in_10[8], in_10[9], in_10[10], in_10[11], in_10[0], out_33[0], out_33[1], out_33[2], out_33[3], out_33[4], out_33[5], out_33[6], out_33[7], out_33[8], out_33[9]
  Button button_2 (.out(button_2_out));
  Clock clock_3 (.out(clock_3_out));
  Demultiplexer #(.select(3), .width(16)) demultiplexer_1 (
    .out0(demultiplexer_1_out0), .out1(demultiplexer_1_out1), .out2(demultiplexer_1_out2),
    .out3(demultiplexer_1_out3), .out4(demultiplexer_1_out4), .out5(demultiplexer_1_out5),
    .out6(demultiplexer_1_out6), .out7(demultiplexer_1_out7), .in(in_26), .sel(ADDRESS));
  RAM #(.addrWidth(14), .clearpin("true"), .dataWidth(16), .trigger("falling"), .\type ("nonvolatile")) ram_1 (
    .addr(adress), .we(write), .oe(read), .clk(clock_3_out), .din(inputt), .dout(display), .clr(reset_out));
  // Shift_Register #(.trigger("falling"), .width(16)) shift_register_2: pin names not known; wires that end beside it: out_33[13], out_33[14], out_33[15], button_2_out, in_17, 1'b0, clock_2_out, demultiplexer_1_out0, demultiplexer_1_out1, demultiplexer_1_out2, demultiplexer_1_out3, demultiplexer_1_out4, demultiplexer_1_out5, demultiplexer_1_out6, demultiplexer_1_out7, shift_register_2_p16, shift_register_2_p17, shift_register_2_p18, shift_register_2_p19, shift_register_2_p20, shift_register_2_p21, shift_register_2_p22, shift_register_2_p23
  LedBar #(.matrixcols(16)) ledbar_2 (
    .led0(out_33[15]), .led1(out_33[14]), .led2(out_33[13]), .led3(out_33[12]), .led4(out_33[11]),
    .led5(out_33[10]), .led6(out_33[9]), .led7(out_33[8]), .led8(out_33[7]), .led9(out_33[6]),
    .led10(out_33[5]), .led11(out_33[4]), .led12(out_33[3]), .led13(out_33[2]), .led14(out_33[1]),
    .led15(out_33[0]));
  LedBar #(.matrixcols(16)) ledbar_3 (
    .led0(out_36[15]), .led1(out_36[14]), .led2(out_36[13]), .led3(out_36[12]), .led4(out_36[11]),
    .led5(out_36[10]), .led6(out_36[9]), .led7(out_36[8]), .led8(out_36[7]), .led9(out_36[6]),
    .led10(out_36[5]), .led11(out_36[4]), .led12(out_36[3]), .led13(out_36[2]), .led14(out_36[1]),
    .led15(out_36[0]));
  Clock clock_4 (.out(clock_4_out));
  Button button_3 (.out(button_3_out));
  LedBar #(.matrixcols(16)) ledbar_4 (
    .led0(inpuut[15]), .led1(inpuut[14]), .led2(inpuut[13]), .led3(inpuut[12]), .led4(inpuut[11]),
    .led5(inpuut[10]), .led6(inpuut[9]), .led7(inpuut[8]), .led8(inpuut[7]), .led9(inpuut[6]),
    .led10(inpuut[5]), .led11(inpuut[4]), .led12(inpuut[3]), .led13(inpuut[2]), .led14(inpuut[1]),
    .led15(inpuut[0]));
  Multiplexer #(.select(3), .width(16)) multiplexer_1 (
    .in0(shift_register_2_p16), .in1(shift_register_2_p17), .in2(shift_register_2_p18),
    .in3(shift_register_2_p19), .in4(shift_register_2_p20), .in5(shift_register_2_p21),
    .in6(shift_register_2_p22), .in7(shift_register_2_p23), .out(out_36), .sel(ADDRESS));
  Demultiplexer #(.select(4)) demultiplexer_2 (
    .out0(demultiplexer_2_out0[0]), .out1(demultiplexer_2_out0[1]), .out2(demultiplexer_2_out0[2]),
    .out3(demultiplexer_2_out0[3]), .out4(demultiplexer_2_out0[4]), .out5(demultiplexer_2_out0[5]),
    .out6(demultiplexer_2_out0[6]), .out7(demultiplexer_2_out0[7]), .out8(demultiplexer_2_out0[8]),
    .out9(demultiplexer_2_out0[9]), .out10(demultiplexer_2_out0[10]), .out11(demultiplexer_2_out0[11]),
    .out12(demultiplexer_2_out0[12]), .out13(demultiplexer_2_out0[13]), .out14(demultiplexer_2_out0[14]),
    .out15(demultiplexer_2_out0[15]), .in(in_3), .sel(in_5));
  Register #(.trigger("falling"), .width(16)) register_1 (
    .D(in_7), .en(in_9), .clk(clock_4_out), .Q(out_34), .clr(button_3_out));
  Demultiplexer #(.select(3)) demultiplexer_3 (
    .out0(demultiplexer_3_out0), .out1(demultiplexer_3_out1), .out2(demultiplexer_3_out2),
    .out3(demultiplexer_3_out3), .out4(demultiplexer_3_out4), .out5(demultiplexer_3_out5),
    .out6(demultiplexer_3_out6), .out7(demultiplexer_3_out7), .in(load), .sel(adddress));
  Demultiplexer #(.select(3), .width(16)) demultiplexer_4 (
    .out0(demultiplexer_4_out0), .out1(demultiplexer_4_out1), .out2(demultiplexer_4_out2),
    .out3(demultiplexer_4_out3), .out4(demultiplexer_4_out4), .out5(demultiplexer_4_out5),
    .out6(demultiplexer_4_out6), .out7(demultiplexer_4_out7), .in(inpuut), .sel(adddress));
  Clock clock_5 (.out(clock_5_out));
  LED led_2 (.in(clock_5_out));
  Register #(.trigger("falling"), .width(16)) register_2 (
    .D(demultiplexer_4_out0), .en(demultiplexer_3_out0), .clk(clock_5_out), .Q(register_2_q), .clr(in_11));
  Register #(.trigger("falling"), .width(16)) register_3 (
    .D(demultiplexer_4_out1), .en(demultiplexer_3_out1), .clk(clock_5_out), .Q(register_3_q), .clr(in_11));
  Register #(.trigger("falling"), .width(16)) register_4 (
    .D(demultiplexer_4_out2), .en(demultiplexer_3_out2), .clk(clock_5_out), .Q(register_4_q), .clr(in_11));
  Register #(.trigger("falling"), .width(16)) register_5 (
    .D(demultiplexer_4_out3), .en(demultiplexer_3_out3), .clk(clock_5_out), .Q(register_5_q), .clr(in_11));
  Register #(.trigger("falling"), .width(16)) register_6 (
    .D(demultiplexer_4_out4), .en(demultiplexer_3_out4), .clk(clock_5_out), .Q(register_6_q), .clr(in_11));
  Register #(.trigger("falling"), .width(16)) register_7 (
    .D(demultiplexer_4_out5), .en(demultiplexer_3_out5), .clk(clock_5_out), .Q(register_7_q), .clr(in_11));
  Register #(.trigger("falling"), .width(16)) register_8 (
    .D(demultiplexer_4_out6), .en(demultiplexer_3_out6), .clk(clock_5_out), .Q(register_8_q), .clr(in_11));
  Register #(.trigger("falling"), .width(16)) register_9 (
    .D(demultiplexer_4_out7), .en(demultiplexer_3_out7), .clk(clock_5_out), .Q(register_9_q), .clr(in_11));
  LedBar #(.matrixcols(16)) ledbar_5 (
    .led0(outpput[15]), .led1(outpput[14]), .led2(outpput[13]), .led3(outpput[12]), .led4(outpput[11]),
    .led5(outpput[10]), .led6(outpput[9]), .led7(outpput[8]), .led8(outpput[7]), .led9(outpput[6]),
    .led10(outpput[5]), .led11(outpput[4]), .led12(outpput[3]), .led13(outpput[2]), .led14(outpput[1]),
    .led15(outpput[0]));
  Multiplexer #(.select(3), .width(16)) multiplexer_2 (
    .in0(register_2_q), .in1(register_3_q), .in2(register_4_q), .in3(register_5_q), .in4(register_6_q),
    .in5(register_7_q), .in6(register_8_q), .in7(register_9_q), .out(outpput), .sel(adddress));
  Hex_Digit_Display hex_digit_display_1 (.value(in_2));  // open: dp
  _7_Segment_Display u_7_segment_display_1 (
    .g(in_6[5]), .f(in_6[6]), .a(in_6[0]), .b(in_6[1]), .e(in_6[4]), .d(in_6[3]), .c(in_6[2]), .dp(in_8));
  Multiplexer #(.select(2), .width(16)) multiplexer_3 (
    .in0(addresss), .in1(in_18), .in2(in_19), .in3(adder_1_out), .out(multiplexer_3_out), .sel(in_25));
  Register #(.trigger("falling"), .width(16)) register_10 (
    .D(multiplexer_3_out), .en(PROGRAM_COUNTER), .clk(clock_6_out), .Q(addresss), .clr(in_21));
  Clock clock_6 (.out(clock_6_out));
  Hex_Digit_Display #(.decimalPoint("false")) hex_digit_display_2 (.value(addresss[15:12]));
  Hex_Digit_Display #(.decimalPoint("false")) hex_digit_display_3 (.value(addresss[11:8]));
  Hex_Digit_Display #(.decimalPoint("false")) hex_digit_display_4 (.value(addresss[7:4]));
  Hex_Digit_Display #(.decimalPoint("false")) hex_digit_display_5 (.value(addresss[3:0]));
  Adder #(.width(16)) adder_1 (.a(addresss), .b(in_20), .out(adder_1_out));  // open: cin, cout
  Clock clock_7 (.out(clock_7_out));
  Counter #(.max('h3fff), .width(14)) counter_1 (
    .clr(in_12), .load(in_13), .up(in_14), .count(not_1_out), .clk(clock_7_out), .D(in_19[13:0]),
    .Q({counter_1_q_2, counter_1_q}));  // open: carry
  not not_1 (not_1_out, in_13);
  Hex_Digit_Display #(.decimalPoint("false")) hex_digit_display_6 (.value({in_16, counter_1_q_2}));
  Hex_Digit_Display #(.decimalPoint("false")) hex_digit_display_7 (.value(counter_1_q[11:8]));
  Hex_Digit_Display #(.decimalPoint("false")) hex_digit_display_8 (.value(counter_1_q[7:4]));
  Hex_Digit_Display #(.decimalPoint("false")) hex_digit_display_9 (.value(counter_1_q[3:0]));

  assign in_22 = in_19[15:14];

  // Notes on the sheet:
  //   incorrect
  //   Hexadecimal format
  //   addresss
  //   Unconventional vs Conventional Counter
  //   Hexadecimal format
  //   addresss
endmodule
